# Fritzing sketch Schematics (saved by Fritzing 0.9.3b)
breadboards: 1

parts:
  Part1 = Arduino Uno (Rev3)
  C1 = Electrolytic Capacitor [capacitance=100µF package="100 mil [THT, electrolytic]"]
  R1 = Resistor [tolerance=±5% resistance=1k package=THT]
  R2 = Rotary Potentiometer (Small) [maximum_resistance=10kΩ package=THT]
  LED1 = smd LED [color="Red (633nm)" package="0805 [SMD]"]
  R3 = Resistor [tolerance=±5% resistance=220 package=THT]
  S1 = Pushbutton [package="[THT]"]
  R4 = Resistor [tolerance=±5% resistance=220 package=THT]
  OLED_I2C1 = OLED 128x64 I2C Monochrome Display

nets:
  N1: Part1.A0, R2.wiper
  N2: Part1.A4/SDA, OLED_I2C1.SDA
  N3: Part1.A5/SCL, OLED_I2C1.SCK
  N4: Part1.D10_PWM/SS, R1.Pin_1
  GND: Part1.GND, C1.+, R2.leg1, LED1.cathode, R4.Pin_0, OLED_I2C1.GND
  N5: Part1.D2, S1.Pin_1, S1.Pin_2, R4.Pin_1
  5V: Part1.5V, R2.leg2, S1.Pin_3, S1.Pin_4, OLED_I2C1.VDD
  N6: C1.-, R1.Pin_0
  N7: LED1.anode, R3.Pin_1
